// Logisim project ALU.circ as structural Verilog: 9 circuits, main circuit main
module main (
  input  [31:0] a,
  input  [31:0] b,
  input  [3:0] aluop,
  input  output_inverted,
  input  output_inc,
  input  clk,
  input  rst,
  output [31:0] res_low,
  output [31:0] res_high,
  output done
);

  wire and_2_out, comparator_1_eq, comparator_2_eq, comparator_3_eq, not_1_out, not_2_out, or_2_out;
  wire [31:0] multiplexer_3_out, multiplexer_4_out, register_1_q, register_2_q;
  wire [63:0] adder_1_out, adder_2_out, and_1_out, bit_extender_1_out, bit_extender_2_out, c3_quotient,
       c9_res, c10_res, c11_res, c12_res, multiplexer_1_out, multiplexer_2_out, not_3_out, or_1_out,
       subtractor_1_out, undriven, undriven_2, xor_1_out;

  assign bit_extender_1_out = {{32{1'b0}}, a};  // Bit_Extender bit_extender_1
  assign bit_extender_2_out = {{32{1'b0}}, b};  // Bit_Extender bit_extender_2
  Comparator #(.mode("unsigned"), .width(4)) comparator_1 (
    .a(aluop), .b(4'b0011), .eq(comparator_1_eq));  // open: gt, lt
  Register #(.width(32)) register_1 (.D(a), .clk(clk), .Q(register_1_q));  // open: en, clr
  Register #(.width(32)) register_2 (.D(b), .clk(clk), .Q(register_2_q));  // open: en, clr
  Adder #(.width(64)) adder_1 (.a(bit_extender_1_out), .b(bit_extender_2_out), .out(adder_1_out));  // open: cin, cout
  Subtractor #(.width(64)) subtractor_1 (
    .a(bit_extender_1_out), .b(bit_extender_2_out), .out(subtractor_1_out));  // open: bin, bout
  assign and_1_out = bit_extender_1_out & bit_extender_2_out;  // AND_Gate and_1, 64 bits wide
  assign or_1_out = bit_extender_1_out | bit_extender_2_out;  // OR_Gate or_1, 64 bits wide
  assign xor_1_out = bit_extender_1_out ^ bit_extender_2_out;  // XOR_Gate xor_1, 64 bits wide
  Comparator #(.mode("unsigned"), .width(32)) comparator_2 (
    .a(register_1_q), .b(a), .eq(comparator_2_eq));  // open: gt, lt
  Comparator #(.mode("unsigned"), .width(32)) comparator_3 (
    .a(register_2_q), .b(b), .eq(comparator_3_eq));  // open: gt, lt
  not not_1 (not_1_out, comparator_2_eq);
  not not_2 (not_2_out, comparator_3_eq);
  CLO c7 ();  // open: in1, S, clk, En, rst, cnt, D
  CLZ c8 ();  // open: in1, S, clk, En, rst, cnt, D
  S_L_L c9 (.A(a), .shamt(b[4:0]), .res(c9_res));
  S_R_L c10 (.A(a), .shamt(b[4:0]), .res(c10_res));
  S_R_A c11 (.A(a), .shamt(b[4:0]), .res(c11_res));
  ROTR2 c12 (.A(a), .shamt(b[4:0]), .res(c12_res));
  or or_2 (or_2_out, not_1_out, not_2_out);
  and and_2 (and_2_out, or_2_out, comparator_1_eq);
  divisor c3 (
    .divisor(b), .dividend(a), .start(and_2_out), .clk(clk), .quotient(c3_quotient[31:0]),
    .remainder(c3_quotient[63:32]), .done(done));
  Multiplexer #(.select(4), .width(64)) multiplexer_1 (
    .in0(adder_1_out), .in1(subtractor_1_out), .in3(c3_quotient), .in4(and_1_out), .in5(or_1_out),
    .in6(xor_1_out), .in7(undriven), .in8(undriven_2), .in9(c9_res), .in10(c10_res), .in11(c11_res),
    .in12(c12_res), .out(multiplexer_1_out), .sel(aluop));  // open: in2, in13, in14, in15
  assign not_3_out = ~multiplexer_1_out;  // NOT_Gate not_3, 64 bits wide
  Multiplexer #(.width(64)) multiplexer_2 (
    .in0(multiplexer_1_out), .in1(not_3_out), .out(multiplexer_2_out), .sel(output_inverted));
  Adder #(.width(64)) adder_2 (
    .a(multiplexer_2_out), .b({64{1'b0}}), .out(adder_2_out), .cin(output_inc));  // open: cout
  Multiplexer #(.width(32)) multiplexer_3 (.in0(adder_2_out[31:0]), .out(multiplexer_3_out), .sel(rst));  // open: in1
  Multiplexer #(.width(32)) multiplexer_4 (.in0(adder_2_out[63:32]), .out(multiplexer_4_out), .sel(rst));  // open: in1
  Register #(.width(32)) register_3 (.D(multiplexer_3_out), .clk(clk), .Q(res_low), .clr(rst));  // open: en
  Register #(.width(32)) register_4 (.D(multiplexer_4_out), .clk(clk), .Q(res_high), .clr(rst));  // open: en

  // Notes on the sheet:
  //   a: initial=0x866cf10c
  //   b: initial=0x1cfc7a39
  //   aluop: initial=0x9
endmodule

module divisor (
  input  [31:0] divisor,
  input  [31:0] dividend,
  input  start,
  input  clk,
  output [31:0] quotient,
  output [31:0] remainder,
  output done
);

  wire and_1_out, bitselector_1_out, comparator_1_eq, comparator_2_lt, not_1_out, not_2_out;
  wire [6:0] counter_q, multiplexer_4_out, multiplexer_8_out, subtractor_1_out;
  wire [31:0] A_q, adder_1_out, B_q, bit_extender_1_out, multiplexer_1_out, multiplexer_2_out,
       multiplexer_3_out, multiplexer_5_out, multiplexer_6_out, multiplexer_7_out, multiplexer_9_out,
       multiplexer_10_out, or_1_out, Q_q, shifter_1_out, shifter_2_out, subtractor_2_out;

  Multiplexer #(.width(32)) multiplexer_1 (
    .in0(multiplexer_9_out), .in1({32{1'b0}}), .out(multiplexer_1_out), .sel(start));
  Multiplexer #(.width(32)) multiplexer_2 (.in0(B_q), .in1(divisor), .out(multiplexer_2_out), .sel(start));
  Multiplexer #(.width(32)) multiplexer_3 (
    .in0(multiplexer_10_out), .in1(dividend), .out(multiplexer_3_out), .sel(start));
  Multiplexer #(.width(7)) multiplexer_4 (
    .in0(multiplexer_8_out), .in1(7'b0100000), .out(multiplexer_4_out), .sel(start));
  Subtractor #(.width(7)) subtractor_1 (.a(counter_q), .b(7'b0000001), .out(subtractor_1_out));  // open: bin, bout
  Multiplexer #(.width(32)) multiplexer_5 (.in0(multiplexer_1_out), .in1(A_q), .out(multiplexer_5_out), .sel(done));
  Multiplexer #(.width(32)) multiplexer_6 (.in0(multiplexer_2_out), .in1(B_q), .out(multiplexer_6_out), .sel(done));
  Multiplexer #(.width(32)) multiplexer_7 (.in0(multiplexer_3_out), .in1(Q_q), .out(multiplexer_7_out), .sel(done));
  Register #(.width(32)) A (.D(multiplexer_5_out), .en(1'b1), .clk(clk), .Q(A_q));  // open: clr
  Register #(.width(32)) B (.D(multiplexer_6_out), .en(1'b1), .clk(clk), .Q(B_q));  // open: clr
  Register #(.width(32)) Q (.D(multiplexer_7_out), .en(1'b1), .clk(clk), .Q(Q_q));  // open: clr
  Register #(.width(7)) counter (.D(multiplexer_4_out), .en(1'b1), .clk(clk), .Q(counter_q));  // open: clr
  Shifter #(.width(32)) shifter_1 (.in(A_q), .\dist (5'b00001), .out(shifter_1_out));
  BitSelector #(.width(32)) bitselector_1 (.in(Q_q), .out(bitselector_1_out), .sel({5{1'b1}}));
  Comparator #(.mode("unsigned"), .width(7)) comparator_1 (
    .a(counter_q), .b({7{1'b0}}), .eq(comparator_1_eq));  // open: gt, lt
  assign bit_extender_1_out = {{31{1'b0}}, bitselector_1_out};  // Bit_Extender bit_extender_1
  Adder #(.width(32)) adder_1 (.a(shifter_1_out), .b(bit_extender_1_out), .out(adder_1_out));  // open: cin, cout
  Shifter #(.width(32)) shifter_2 (.in(Q_q), .\dist (5'b00001), .out(shifter_2_out));
  Multiplexer #(.width(7)) multiplexer_8 (
    .in0(subtractor_1_out), .in1(counter_q), .out(multiplexer_8_out), .sel(comparator_1_eq));
  Subtractor #(.width(32)) subtractor_2 (.a(adder_1_out), .b(B_q), .out(subtractor_2_out));  // open: bin, bout
  Comparator #(.mode("unsigned"), .width(32)) comparator_2 (
    .a(adder_1_out), .b(B_q), .lt(comparator_2_lt));  // open: gt, eq
  not not_1 (not_1_out, comparator_2_lt);
  assign or_1_out = shifter_2_out | 32'h1;  // OR_Gate or_1, 32 bits wide
  and and_1 (and_1_out, comparator_1_eq, not_2_out);
  not not_2 (not_2_out, start);
  Multiplexer #(.width(32)) multiplexer_9 (
    .in0(adder_1_out), .in1(subtractor_2_out), .out(multiplexer_9_out), .sel(not_1_out));
  Multiplexer #(.width(32)) multiplexer_10 (
    .in0(shifter_2_out), .in1(or_1_out), .out(multiplexer_10_out), .sel(not_1_out));
  Multiplexer #(.width(32)) multiplexer_11 (.in1(Q_q), .out(quotient), .sel(and_1_out));  // open: in0
  Multiplexer #(.width(32)) multiplexer_12 (.in1(A_q), .out(remainder), .sel(and_1_out));  // open: in0
  Multiplexer multiplexer_13 (.in0(1'b0), .in1(1'b1), .out(done), .sel(and_1_out));

  // Notes on the sheet:
  //   divisor: initial=0xc4018d88
  //   dividend: initial=0x82fbf905
  //   clk: initial=0x1
endmodule

module ROTR (
  input  [31:0] A,
  input  [4:0] shamt,
  output [63:0] res
);

  wire [1:0] lsb2;
  wire [3:0] lsb4;
  wire [7:0] lsb8;
  wire [15:0] lsb16;
  wire [47:0] shift_16;
  wire [55:0] shift_8;
  wire [59:0] shift_4;
  wire [61:0] shift_2;
  wire [63:0] extended_64, stage_16;

  assign extended_64 = {{32{1'b0}}, A};  // Bit_Extender bit_extender_1
  Multiplexer #(.width(64)) multiplexer_1 (
    .in0({shift_16, lsb16}), .in1({lsb16, shift_16}), .out(stage_16), .sel(shamt[4]));
  Multiplexer #(.width(64)) multiplexer_2 (
    .in0(extended_64), .in1({extended_64[0], extended_64[63:1]}), .out({shift_2, lsb2}), .sel(shamt[0]));
  Multiplexer #(.width(64)) multiplexer_3 (
    .in0({shift_2, lsb2}), .in1({lsb2, shift_2}), .out({shift_4, lsb4}), .sel(shamt[1]));
  Multiplexer #(.width(64)) multiplexer_4 (
    .in0({shift_4, lsb4}), .in1({lsb4, shift_4}), .out({shift_8, lsb8}), .sel(shamt[2]));
  Multiplexer #(.width(64)) multiplexer_5 (
    .in0({shift_8, lsb8}), .in1({lsb8, shift_8}), .out({shift_16, lsb16}), .sel(shamt[3]));
  assign res[31:0] = stage_16[31:0] | stage_16[63:32];  // OR_Gate or_1, 32 bits wide

  assign res[63:32] = {32{1'b0}};

  // Other names for the same wires on the sheet: b0 = shamt[0]; b1 = shamt[1]; b2 = shamt[2]; b3 = shamt[3];
  //   b4 = shamt[4]; shift_1[63:0] = {extended_64[0], extended_64[63:1]}; lsb1 = extended_64[0];
  //   stage_1[63:0] = {shift_2, lsb2}; stage_2[63:0] = {shift_4, lsb4}; shift_4[63:60] = lsb4;
  //   stage_4[63:0] = {shift_8, lsb8}; shift_8[63:56] = lsb8; stage_8[63:0] = {shift_16, lsb16};
  //   shift_2[63:62] = lsb2; shift_16[63:48] = lsb16
endmodule

module S_R_A (
  input  [31:0] A,
  input  [4:0] shamt,
  output [63:0] res
);

  wire [1:0] stage_1;
  wire [3:0] stage_2;
  wire [7:0] stage_4;
  wire [15:0] stage_8;
  wire [63:0] extended_64, shift_2, shift_4, shift_8, shift_16;

  assign extended_64 = {{32{A[31]}}, A};  // Bit_Extender bit_extender_1
  Multiplexer #(.width(64)) multiplexer_1 (
    .in0({shift_16[63], shift_16[46:0], stage_8}), .in1({{17{shift_16[63]}}, shift_16[46:0]}), .out(res),
    .sel(shamt[4]));
  Multiplexer #(.width(64)) multiplexer_2 (
    .in0(extended_64), .in1({{2{extended_64[63]}}, extended_64[62:1]}),
    .out({shift_2[63], shift_2[60:0], stage_1}), .sel(shamt[0]));
  Multiplexer #(.width(64)) multiplexer_3 (
    .in0({shift_2[63], shift_2[60:0], stage_1}), .in1({{3{shift_2[63]}}, shift_2[60:0]}),
    .out({shift_4[63], shift_4[58:0], stage_2}), .sel(shamt[1]));
  Multiplexer #(.width(64)) multiplexer_4 (
    .in0({shift_4[63], shift_4[58:0], stage_2}), .in1({{5{shift_4[63]}}, shift_4[58:0]}),
    .out({shift_8[63], shift_8[54:0], stage_4}), .sel(shamt[2]));
  Multiplexer #(.width(64)) multiplexer_5 (
    .in0({shift_8[63], shift_8[54:0], stage_4}), .in1({{9{shift_8[63]}}, shift_8[54:0]}),
    .out({shift_16[63], shift_16[46:0], stage_8}), .sel(shamt[3]));

  // Other names for the same wires on the sheet: b0 = shamt[0]; b1 = shamt[1]; b2 = shamt[2]; b3 = shamt[3];
  //   b4 = shamt[4]; shift_1[63:0] = {{2{extended_64[63]}}, extended_64[62:1]};
  //   stage_1[63:2] = {shift_2[63], shift_2[60:0]}; shift_2[62:61] = {2{shift_2[63]}};
  //   stage_2[63:4] = {shift_4[63], shift_4[58:0]}; shift_4[62:59] = {4{shift_4[63]}};
  //   stage_4[63:8] = {shift_8[63], shift_8[54:0]}; shift_8[62:55] = {8{shift_8[63]}};
  //   stage_8[63:16] = {shift_16[63], shift_16[46:0]}; shift_16[62:47] = {16{shift_16[63]}}; stage_16[63:0] = res
endmodule

module S_R_L (
  input  [31:0] A,
  input  [4:0] shamt,
  output [63:0] res
);

  wire [1:0] stage_1;
  wire [3:0] stage_2;
  wire [7:0] stage_4;
  wire [15:0] stage_8;
  wire [47:0] shift_16;
  wire [55:0] shift_8;
  wire [59:0] shift_4;
  wire [61:0] shift_2;
  wire [63:0] extended_64;

  assign extended_64 = {{32{1'b0}}, A};  // Bit_Extender bit_extender_1
  Multiplexer #(.width(64)) multiplexer_1 (
    .in0({shift_16, stage_8}), .in1({{16{1'b0}}, shift_16}), .out(res), .sel(shamt[4]));
  Multiplexer #(.width(64)) multiplexer_2 (
    .in0(extended_64), .in1({1'b0, extended_64[63:1]}), .out({shift_2, stage_1}), .sel(shamt[0]));
  Multiplexer #(.width(64)) multiplexer_3 (
    .in0({shift_2, stage_1}), .in1({2'b00, shift_2}), .out({shift_4, stage_2}), .sel(shamt[1]));
  Multiplexer #(.width(64)) multiplexer_4 (
    .in0({shift_4, stage_2}), .in1({4'b0000, shift_4}), .out({shift_8, stage_4}), .sel(shamt[2]));
  Multiplexer #(.width(64)) multiplexer_5 (
    .in0({shift_8, stage_4}), .in1({{8{1'b0}}, shift_8}), .out({shift_16, stage_8}), .sel(shamt[3]));

  // Other names for the same wires on the sheet: b0 = shamt[0]; b1 = shamt[1]; b2 = shamt[2]; b3 = shamt[3];
  //   b4 = shamt[4]; shift_1[62:0] = extended_64[63:1]; stage_1[63:2] = shift_2; stage_2[63:4] = shift_4;
  //   stage_4[63:8] = shift_8; stage_8[63:16] = shift_16; stage_16[63:0] = res
endmodule

module S_L_L (
  input  [31:0] A,
  input  [4:0] shamt,
  output [63:0] res
);

  wire [63:0] extended_64;
  wire [63:2] shift_2;
  wire [63:4] shift_4;
  wire [63:8] shift_8;
  wire [63:16] shift_16;
  wire [63:48] stage_8;
  wire [63:56] stage_4;
  wire [63:60] stage_2;
  wire [63:62] stage_1;

  assign extended_64 = {{32{1'b0}}, A};  // Bit_Extender bit_extender_1
  Multiplexer #(.width(64)) multiplexer_1 (
    .in0({stage_8, shift_16}), .in1({shift_16, {16{1'b0}}}), .out(res), .sel(shamt[4]));
  Multiplexer #(.width(64)) multiplexer_2 (
    .in0(extended_64), .in1({extended_64[62:0], 1'b0}), .out({stage_1, shift_2}), .sel(shamt[0]));
  Multiplexer #(.width(64)) multiplexer_3 (
    .in0({stage_1, shift_2}), .in1({shift_2, 2'b00}), .out({stage_2, shift_4}), .sel(shamt[1]));
  Multiplexer #(.width(64)) multiplexer_4 (
    .in0({stage_2, shift_4}), .in1({shift_4, 4'b0000}), .out({stage_4, shift_8}), .sel(shamt[2]));
  Multiplexer #(.width(64)) multiplexer_5 (
    .in0({stage_4, shift_8}), .in1({shift_8, {8{1'b0}}}), .out({stage_8, shift_16}), .sel(shamt[3]));

  // Other names for the same wires on the sheet: b0 = shamt[0]; b1 = shamt[1]; b2 = shamt[2]; b3 = shamt[3];
  //   b4 = shamt[4]; shift_1[63:1] = extended_64[62:0]; stage_2[59:0] = shift_4; stage_4[55:0] = shift_8;
  //   stage_8[47:0] = shift_16; stage_1[61:0] = shift_2; stage_16[63:0] = res
endmodule

module CLO (
  input  [31:0] in1,
  input  S,
  input  clk,
  input  En,
  input  rst,
  output [4:0] cnt,
  output D
);

  wire CBO, FINAL, INIT, not_1_out, not_2_out, not_3_out, not_4_out, not_5_out, or_1_out, or_2_out, or_3_out,
       or_4_out, R0_bit0, RN_eq_0, SHIFT, T0, T1, T2, T3, T4, T5;
  wire [4:0] adder_1_out, controlled_buffer_1_out, R1_q, RN_dec, RN_q;
  wire [31:0] controlled_buffer_3_out, R0_q;
  wire [63:0] c71_res;

  or or_1 (or_1_out, T0, SHIFT);
  D_Flip_Flop u_INIT (.D(T4), .clk(clk), .Q(INIT), .preset(rst));  // open: Qn, reset
  D_Flip_Flop u_CBO (.D(or_1_out), .clk(clk), .Q(CBO), .reset(rst));  // open: Qn, preset
  D_Flip_Flop u_SHIFT (.D(T5), .clk(clk), .Q(SHIFT), .reset(rst));  // open: Qn, preset
  D_Flip_Flop u_FINAL (.D(T1), .clk(clk), .Q(FINAL), .reset(rst));  // open: Qn, preset
  not not_1 (not_1_out, RN_eq_0);
  not not_2 (not_2_out, RN_eq_0);
  not not_3 (not_3_out, R0_bit0);
  not not_4 (not_4_out, S);
  not not_5 (not_5_out, RN_eq_0);
  and and_1 (T0, INIT, S);
  and and_2 (T1, CBO, En, RN_eq_0);
  and and_3 (T2, CBO, not_1_out, R0_bit0);
  and and_4 (T3, CBO, not_2_out, not_3_out);
  and and_5 (T4, INIT, not_4_out);
  and and_6 (T5, CBO, not_5_out);
  assign controlled_buffer_1_out = T0 ? {5{1'b0}} : 5'bz;  // Controlled_Buffer controlled_buffer_1
  assign controlled_buffer_1_out = SHIFT ? RN_dec : 5'bz;  // Controlled_Buffer controlled_buffer_2
  or or_2 (or_2_out, T0, SHIFT);
  Register #(.width(5)) RN (.D(controlled_buffer_1_out), .en(or_2_out), .clk(clk), .Q(RN_q));  // open: clr
  or or_3 (or_3_out, T0, SHIFT);
  assign controlled_buffer_3_out = T0 ? in1 : 32'bz;  // Controlled_Buffer controlled_buffer_3
  assign controlled_buffer_3_out = SHIFT ? c71_res[31:0] : 32'bz;  // Controlled_Buffer controlled_buffer_4
  Subtractor #(.width(5)) subtractor_1 (.a(RN_q), .b(5'b00001), .out(RN_dec));  // open: bin, bout
  Comparator #(.width(5)) comparator_1 (.a(RN_q), .b({5{1'b0}}), .eq(RN_eq_0));  // open: gt, lt
  Register #(.width(32)) R0 (.D(controlled_buffer_3_out), .en(or_3_out), .clk(clk), .Q(R0_q));  // open: clr
  or or_4 (or_4_out, T3, T0);
  and and_7 (R0_bit0, 1'b1, R0_q[0]);
  Register #(.width(5)) R1 (.D(adder_1_out), .en(T2), .clk(clk), .Q(R1_q), .clr(or_4_out));
  Register #(.width(5)) R2 (.D(R1_q), .en(T1), .clk(clk), .Q(cnt), .clr(rst));
  Register #(.width(1)) RD (.D(1'b1), .en(T1), .clk(clk), .Q(D), .clr(T0));
  S_R_L c71 (.A(R0_q), .shamt(5'b00001), .res(c71_res));
  Adder #(.width(5)) adder_1 (.a(R1_q), .b(5'b00001), .out(adder_1_out));  // open: cin, cout
endmodule

module CLZ (
  input  [31:0] in1,
  input  S,
  input  clk,
  input  En,
  input  rst,
  output [4:0] cnt,
  output D
);

  wire CBO, FINAL, INIT, not_1_out, not_2_out, not_3_out, not_4_out, not_5_out, not_6_out, or_1_out,
       or_2_out, or_3_out, or_4_out, R0_bit0, RN_eq_0, SHIFT, T0, T1, T2, T3, T4, T5;
  wire [4:0] adder_1_out, controlled_buffer_1_out, R1_q, RN_dec, RN_q;
  wire [31:0] controlled_buffer_3_out, R0_q;
  wire [63:0] c81_res;

  or or_1 (or_1_out, T0, SHIFT);
  D_Flip_Flop u_INIT (.D(T4), .clk(clk), .Q(INIT), .preset(rst));  // open: Qn, reset
  D_Flip_Flop u_CBO (.D(or_1_out), .clk(clk), .Q(CBO), .reset(rst));  // open: Qn, preset
  D_Flip_Flop u_SHIFT (.D(T5), .clk(clk), .Q(SHIFT), .reset(rst));  // open: Qn, preset
  D_Flip_Flop u_FINAL (.D(T1), .clk(clk), .Q(FINAL), .reset(rst));  // open: Qn, preset
  not not_1 (not_1_out, RN_eq_0);
  not not_2 (not_2_out, RN_eq_0);
  not not_3 (not_3_out, R0_bit0);
  not not_4 (not_4_out, S);
  not not_5 (not_5_out, RN_eq_0);
  and and_1 (T0, INIT, S);
  and and_2 (T1, CBO, En, RN_eq_0);
  and and_3 (T2, CBO, not_1_out, R0_bit0);
  and and_4 (T3, CBO, not_2_out, not_3_out);
  and and_5 (T4, INIT, not_4_out);
  and and_6 (T5, CBO, not_5_out);
  assign controlled_buffer_1_out = T0 ? {5{1'b1}} : 5'bz;  // Controlled_Buffer controlled_buffer_1
  assign controlled_buffer_1_out = SHIFT ? RN_dec : 5'bz;  // Controlled_Buffer controlled_buffer_2
  or or_2 (or_2_out, T0, SHIFT);
  Register #(.width(5)) RN (.D(controlled_buffer_1_out), .en(or_2_out), .clk(clk), .Q(RN_q));  // open: clr
  or or_3 (or_3_out, T0, SHIFT);
  assign controlled_buffer_3_out = T0 ? in1 : 32'bz;  // Controlled_Buffer controlled_buffer_3
  assign controlled_buffer_3_out = SHIFT ? c81_res[31:0] : 32'bz;  // Controlled_Buffer controlled_buffer_4
  Subtractor #(.width(5)) subtractor_1 (.a(RN_q), .b(5'b00001), .out(RN_dec));  // open: bin, bout
  Comparator #(.width(5)) comparator_1 (.a(RN_q), .b({5{1'b0}}), .eq(RN_eq_0));  // open: gt, lt
  Register #(.width(32)) R0 (.D(controlled_buffer_3_out), .en(or_3_out), .clk(clk), .Q(R0_q));  // open: clr
  or or_4 (or_4_out, T3, T0);
  not not_6 (not_6_out, R0_q[0]);
  Register #(.width(5)) R1 (.D(adder_1_out), .en(T2), .clk(clk), .Q(R1_q), .clr(or_4_out));
  Register #(.width(5)) R2 (.D(R1_q), .en(T1), .clk(clk), .Q(cnt), .clr(rst));
  and and_7 (R0_bit0, 1'b1, not_6_out);
  Register #(.width(1)) RD (.D(1'b1), .en(T1), .clk(clk), .Q(D), .clr(T0));
  S_R_L c81 (.A(R0_q), .shamt(5'b00001), .res(c81_res));
  Adder #(.width(5)) adder_1 (.a(R1_q), .b(5'b00001), .out(adder_1_out));  // open: cin, cout
endmodule

module ROTR2 (
  input  [31:0] A,
  input  [4:0] shamt,
  output [63:0] res
);

  wire [1:0] lsb2;
  wire [3:0] lsb4;
  wire [7:0] lsb8;
  wire [15:0] lsb16;
  wire [47:0] shift_16;
  wire [55:0] shift_8;
  wire [59:0] shift_4;
  wire [61:0] shift_2;
  wire [63:0] extended_64, stage_16;

  assign extended_64 = {{32{1'b0}}, A};  // Bit_Extender bit_extender_1
  Multiplexer #(.width(64)) multiplexer_1 (
    .in0({shift_16, lsb16}), .in1({lsb16, shift_16}), .out(stage_16), .sel(shamt[4]));
  Multiplexer #(.width(64)) multiplexer_2 (
    .in0(extended_64), .in1({extended_64[0], extended_64[63:1]}), .out({shift_2, lsb2}), .sel(shamt[0]));
  Multiplexer #(.width(64)) multiplexer_3 (
    .in0({shift_2, lsb2}), .in1({lsb2, shift_2}), .out({shift_4, lsb4}), .sel(shamt[1]));
  Multiplexer #(.width(64)) multiplexer_4 (
    .in0({shift_4, lsb4}), .in1({lsb4, shift_4}), .out({shift_8, lsb8}), .sel(shamt[2]));
  Multiplexer #(.width(64)) multiplexer_5 (
    .in0({shift_8, lsb8}), .in1({lsb8, shift_8}), .out({shift_16, lsb16}), .sel(shamt[3]));
  assign res[31:0] = stage_16[31:0] | stage_16[63:32];  // OR_Gate or_1, 32 bits wide

  assign res[63:32] = {32{1'b0}};

  // Other names for the same wires on the sheet: b0 = shamt[0]; b1 = shamt[1]; b2 = shamt[2]; b3 = shamt[3];
  //   b4 = shamt[4]; shift_1[63:0] = {extended_64[0], extended_64[63:1]}; lsb1 = extended_64[0];
  //   stage_1[63:0] = {shift_2, lsb2}; stage_2[63:0] = {shift_4, lsb4}; shift_4[63:60] = lsb4;
  //   stage_4[63:0] = {shift_8, lsb8}; shift_8[63:56] = lsb8; stage_8[63:0] = {shift_16, lsb16};
  //   shift_2[63:62] = lsb2; shift_16[63:48] = lsb16
endmodule
