// Logisim project ALU.circ as structural Verilog: 11 circuits, main circuit main
module main (
  input  [31:0] a,
  input  [31:0] b,
  input  [3:0] aluop,
  input  output_inverted,
  input  output_inc,
  input  clk,
  input  rst,
  output [31:0] res_low,
  output [31:0] res_high,
  output done
);

  wire and_2_out, c2_done, c3_done, comparator_1_eq, comparator_2_eq, comparator_3_eq, comparator_4_eq,
       comparator_4_lt, comparator_5_eq, comparator_5_lt, comparator_6_eq, new_input, not_2_out, not_3_out,
       S_op;
  wire [4:0] c7_cnt, c8_cnt;
  wire [31:0] register_1_q, register_2_q;
  wire [63:0] adder_1_out, and_1_out, bit_extender_1_out, bit_extender_2_out, bit_extender_3_out,
       bit_extender_4_out, bit_extender_5_out, c0_res, c2_res, c3_quotient, c9_res, c10_res, c11_res,
       c12_res, carry_select_adder_1_res, multiplexer_1_out, multiplexer_2_out, not_1_out, not_4_out,
       or_1_out, xor_1_out;

  assign bit_extender_1_out = {{32{1'b0}}, b};  // Bit_Extender bit_extender_1
  assign not_1_out = ~bit_extender_1_out;  // NOT_Gate not_1, 64 bits wide
  assign bit_extender_2_out = {{32{1'b0}}, a};  // Bit_Extender bit_extender_2
  assign bit_extender_3_out = {{32{1'b0}}, b};  // Bit_Extender bit_extender_3
  Register #(.width(32)) register_1 (.D(a), .clk(clk), .Q(register_1_q), .clr(rst));  // open: en
  Register #(.width(32)) register_2 (.D(b), .clk(clk), .Q(register_2_q), .clr(rst));  // open: en
  Carry_Select_Adder c0 (.a(bit_extender_2_out), .b(bit_extender_3_out), .res(c0_res));  // open: c_in
  Carry_Select_Adder carry_select_adder_1 (
    .c_in(1'b1), .a(bit_extender_2_out), .b(not_1_out), .res(carry_select_adder_1_res));
  assign and_1_out = bit_extender_2_out & bit_extender_3_out;  // AND_Gate and_1, 64 bits wide
  assign or_1_out = bit_extender_2_out | bit_extender_3_out;  // OR_Gate or_1, 64 bits wide
  assign xor_1_out = bit_extender_2_out ^ bit_extender_3_out;  // XOR_Gate xor_1, 64 bits wide
  Comparator #(.mode("unsigned"), .width(32)) comparator_1 (
    .a(register_1_q), .b(a), .eq(comparator_1_eq));  // open: gt, lt
  Comparator #(.mode("unsigned"), .width(32)) comparator_2 (
    .a(register_2_q), .b(b), .eq(comparator_2_eq));  // open: gt, lt
  not not_2 (not_2_out, comparator_1_eq);
  not not_3 (not_3_out, comparator_2_eq);
  S_L_L c9 (.A(a), .shamt(b[4:0]), .res(c9_res));
  S_R_L c10 (.A(a), .shamt(b[4:0]), .res(c10_res));
  S_R_A c11 (.A(a), .shamt(b[4:0]), .res(c11_res));
  ROTR2 c12 (.A(a), .shamt(b[4:0]), .res(c12_res));
  or or_2 (new_input, not_2_out, not_3_out);
  and and_2 (and_2_out, new_input, S_op);
  divisor c3 (
    .divisor(b), .dividend(a), .start(and_2_out), .clk(clk), .quotient(c3_quotient[31:0]),
    .remainder(c3_quotient[63:32]), .done(c3_done));
  M_U_L c2 (.a(a), .b(b), .start(and_2_out), .clk(clk), .res(c2_res), .done(c2_done));
  C_L_O c7 (.in1(a), .S(1'b1), .clk(clk), .En(1'b1), .rst(and_2_out), .cnt(c7_cnt));  // open: D
  C_L_Z c8 (.in1(a), .S(1'b1), .clk(clk), .En(1'b1), .rst(and_2_out), .cnt(c8_cnt));  // open: D
  assign bit_extender_4_out = {{59{c7_cnt[4]}}, c7_cnt};  // Bit_Extender bit_extender_4
  assign bit_extender_5_out = {{59{c8_cnt[4]}}, c8_cnt};  // Bit_Extender bit_extender_5
  Multiplexer #(.select(4), .width(64)) multiplexer_1 (
    .in0(c0_res), .in1(carry_select_adder_1_res), .in2(c2_res), .in3(c3_quotient), .in4(and_1_out),
    .in5(or_1_out), .in6(xor_1_out), .in7(bit_extender_4_out), .in8(bit_extender_5_out), .in9(c9_res),
    .in10(c10_res), .in11(c11_res), .in12(c12_res), .out(multiplexer_1_out), .sel(aluop));  // open: in13, in14, in15
  assign not_4_out = ~multiplexer_1_out;  // NOT_Gate not_4, 64 bits wide
  Multiplexer #(.width(64)) multiplexer_2 (
    .in0(multiplexer_1_out), .in1(not_4_out), .out(multiplexer_2_out), .sel(output_inverted));
  Adder #(.width(64)) adder_1 (
    .a(multiplexer_2_out), .b({64{1'b0}}), .out(adder_1_out), .cin(output_inc));  // open: cout
  or or_3 (done, c3_done, c2_done);
  Multiplexer #(.width(32)) multiplexer_3 (.in0(adder_1_out[31:0]), .out(res_low), .sel(rst));  // open: in1
  Multiplexer #(.width(32)) multiplexer_4 (.in0(adder_1_out[63:32]), .out(res_high), .sel(rst));  // open: in1
  Comparator #(.mode("unsigned"), .width(4)) comparator_3 (
    .a(4'b0010), .b(aluop), .eq(comparator_3_eq));  // open: gt, lt
  Comparator #(.mode("unsigned"), .width(4)) comparator_4 (
    .a(aluop), .b(4'b0011), .eq(comparator_4_eq), .lt(comparator_4_lt));  // open: gt
  Comparator #(.mode("unsigned"), .width(4)) comparator_5 (
    .a(aluop), .b(4'b0111), .eq(comparator_5_eq), .lt(comparator_5_lt));  // open: gt
  Comparator #(.mode("unsigned"), .width(4)) comparator_6 (
    .a(aluop), .b(4'b1000), .eq(comparator_6_eq));  // open: gt, lt
  or or_4 (S_op, comparator_3_eq, comparator_5_eq, comparator_6_eq, comparator_4_eq);

  // Notes on the sheet:
  //   a: initial=0x63c530c7
  //   b: initial=0x175c9c2e
  //   aluop: initial=0x2
endmodule

module divisor (
  input  [31:0] divisor,
  input  [31:0] dividend,
  input  start,
  input  clk,
  output [31:0] quotient,
  output [31:0] remainder,
  output done
);

  wire bitselector_1_out, comparator_1_eq, comparator_2_lt, not_1_out, not_2_out;
  wire [6:0] adder_1_out, counter_q, multiplexer_4_out, multiplexer_8_out;
  wire [31:0] A_q, adder_2_out, B_q, bit_extender_1_out, multiplexer_1_out, multiplexer_2_out,
       multiplexer_3_out, multiplexer_5_out, multiplexer_6_out, multiplexer_7_out, multiplexer_9_out,
       multiplexer_10_out, or_1_out, Q_q, shifter_1_out, shifter_2_out, subtractor_1_out;

  Multiplexer #(.width(32)) multiplexer_1 (
    .in0(multiplexer_9_out), .in1({32{1'b0}}), .out(multiplexer_1_out), .sel(start));
  Multiplexer #(.width(32)) multiplexer_2 (.in0(B_q), .in1(divisor), .out(multiplexer_2_out), .sel(start));
  Multiplexer #(.width(32)) multiplexer_3 (
    .in0(multiplexer_10_out), .in1(dividend), .out(multiplexer_3_out), .sel(start));
  Multiplexer #(.width(7)) multiplexer_4 (
    .in0(multiplexer_8_out), .in1({7{1'b0}}), .out(multiplexer_4_out), .sel(start));
  Adder #(.width(7)) adder_1 (.a(counter_q), .b(7'b0000001), .out(adder_1_out));  // open: cin, cout
  Multiplexer #(.width(32)) multiplexer_5 (.in0(multiplexer_1_out), .in1(A_q), .out(multiplexer_5_out), .sel(done));
  Multiplexer #(.width(32)) multiplexer_6 (.in0(multiplexer_2_out), .in1(B_q), .out(multiplexer_6_out), .sel(done));
  Multiplexer #(.width(32)) multiplexer_7 (.in0(multiplexer_3_out), .in1(Q_q), .out(multiplexer_7_out), .sel(done));
  Register #(.width(32)) A (.D(multiplexer_5_out), .en(1'b1), .clk(clk), .Q(A_q));  // open: clr
  Register #(.width(32)) B (.D(multiplexer_6_out), .en(1'b1), .clk(clk), .Q(B_q));  // open: clr
  Register #(.width(32)) Q (.D(multiplexer_7_out), .en(1'b1), .clk(clk), .Q(Q_q));  // open: clr
  Register #(.width(7)) counter (.D(multiplexer_4_out), .en(1'b1), .clk(clk), .Q(counter_q));  // open: clr
  Shifter #(.width(32)) shifter_1 (.in(A_q), .\dist (5'b00001), .out(shifter_1_out));
  BitSelector #(.width(32)) bitselector_1 (.in(Q_q), .out(bitselector_1_out), .sel({5{1'b1}}));
  Comparator #(.mode("unsigned"), .width(7)) comparator_1 (
    .a(counter_q), .b(7'b0100000), .eq(comparator_1_eq));  // open: gt, lt
  assign bit_extender_1_out = {{31{1'b0}}, bitselector_1_out};  // Bit_Extender bit_extender_1
  Adder #(.width(32)) adder_2 (.a(shifter_1_out), .b(bit_extender_1_out), .out(adder_2_out));  // open: cin, cout
  Shifter #(.width(32)) shifter_2 (.in(Q_q), .\dist (5'b00001), .out(shifter_2_out));
  Multiplexer #(.width(7)) multiplexer_8 (
    .in0(adder_1_out), .in1(counter_q), .out(multiplexer_8_out), .sel(comparator_1_eq));
  Subtractor #(.width(32)) subtractor_1 (.a(adder_2_out), .b(B_q), .out(subtractor_1_out));  // open: bin, bout
  Comparator #(.mode("unsigned"), .width(32)) comparator_2 (
    .a(adder_2_out), .b(B_q), .lt(comparator_2_lt));  // open: gt, eq
  not not_1 (not_1_out, comparator_2_lt);
  assign or_1_out = shifter_2_out | 32'h1;  // OR_Gate or_1, 32 bits wide
  and and_1 (done, comparator_1_eq, not_2_out);
  not not_2 (not_2_out, start);
  Multiplexer #(.width(32)) multiplexer_9 (
    .in0(adder_2_out), .in1(subtractor_1_out), .out(multiplexer_9_out), .sel(not_1_out));
  Multiplexer #(.width(32)) multiplexer_10 (
    .in0(shifter_2_out), .in1(or_1_out), .out(multiplexer_10_out), .sel(not_1_out));
  Multiplexer #(.width(32)) multiplexer_11 (.in1(Q_q), .out(quotient), .sel(done));  // open: in0
  Multiplexer #(.width(32)) multiplexer_12 (.in1(A_q), .out(remainder), .sel(done));  // open: in0

  // Notes on the sheet:
  //   divisor: initial=0xc4018d88
  //   dividend: initial=0x82fbf905
  //   clk: initial=0x1
endmodule

module S_R_A (
  input  [31:0] A,
  input  [4:0] shamt,
  output [63:0] res
);

  wire [1:0] stage_1;
  wire [3:0] stage_2;
  wire [7:0] stage_4;
  wire [15:0] stage_8;
  wire [63:0] extended_64, shift_2, shift_4, shift_8, shift_16;

  assign extended_64 = {{32{A[31]}}, A};  // Bit_Extender bit_extender_1
  Multiplexer #(.width(64)) multiplexer_1 (
    .in0({shift_16[63], shift_16[46:0], stage_8}), .in1({{17{shift_16[63]}}, shift_16[46:0]}), .out(res),
    .sel(shamt[4]));
  Multiplexer #(.width(64)) multiplexer_2 (
    .in0(extended_64), .in1({{2{extended_64[63]}}, extended_64[62:1]}),
    .out({shift_2[63], shift_2[60:0], stage_1}), .sel(shamt[0]));
  Multiplexer #(.width(64)) multiplexer_3 (
    .in0({shift_2[63], shift_2[60:0], stage_1}), .in1({{3{shift_2[63]}}, shift_2[60:0]}),
    .out({shift_4[63], shift_4[58:0], stage_2}), .sel(shamt[1]));
  Multiplexer #(.width(64)) multiplexer_4 (
    .in0({shift_4[63], shift_4[58:0], stage_2}), .in1({{5{shift_4[63]}}, shift_4[58:0]}),
    .out({shift_8[63], shift_8[54:0], stage_4}), .sel(shamt[2]));
  Multiplexer #(.width(64)) multiplexer_5 (
    .in0({shift_8[63], shift_8[54:0], stage_4}), .in1({{9{shift_8[63]}}, shift_8[54:0]}),
    .out({shift_16[63], shift_16[46:0], stage_8}), .sel(shamt[3]));

  // Other names for the same wires on the sheet: b0 = shamt[0]; b1 = shamt[1]; b2 = shamt[2]; b3 = shamt[3];
  //   b4 = shamt[4]; shift_1[63:0] = {{2{extended_64[63]}}, extended_64[62:1]};
  //   stage_1[63:2] = {shift_2[63], shift_2[60:0]}; shift_2[62:61] = {2{shift_2[63]}};
  //   stage_2[63:4] = {shift_4[63], shift_4[58:0]}; shift_4[62:59] = {4{shift_4[63]}};
  //   stage_4[63:8] = {shift_8[63], shift_8[54:0]}; shift_8[62:55] = {8{shift_8[63]}};
  //   stage_8[63:16] = {shift_16[63], shift_16[46:0]}; shift_16[62:47] = {16{shift_16[63]}}; stage_16[63:0] = res
endmodule

module S_R_L (
  input  [31:0] A,
  input  [4:0] shamt,
  output [63:0] res
);

  wire [1:0] stage_1;
  wire [3:0] stage_2;
  wire [7:0] stage_4;
  wire [15:0] stage_8;
  wire [47:0] shift_16;
  wire [55:0] shift_8;
  wire [59:0] shift_4;
  wire [61:0] shift_2;
  wire [63:0] extended_64;

  assign extended_64 = {{32{1'b0}}, A};  // Bit_Extender bit_extender_1
  Multiplexer #(.width(64)) multiplexer_1 (
    .in0({shift_16, stage_8}), .in1({{16{1'b0}}, shift_16}), .out(res), .sel(shamt[4]));
  Multiplexer #(.width(64)) multiplexer_2 (
    .in0(extended_64), .in1({1'b0, extended_64[63:1]}), .out({shift_2, stage_1}), .sel(shamt[0]));
  Multiplexer #(.width(64)) multiplexer_3 (
    .in0({shift_2, stage_1}), .in1({2'b00, shift_2}), .out({shift_4, stage_2}), .sel(shamt[1]));
  Multiplexer #(.width(64)) multiplexer_4 (
    .in0({shift_4, stage_2}), .in1({4'b0000, shift_4}), .out({shift_8, stage_4}), .sel(shamt[2]));
  Multiplexer #(.width(64)) multiplexer_5 (
    .in0({shift_8, stage_4}), .in1({{8{1'b0}}, shift_8}), .out({shift_16, stage_8}), .sel(shamt[3]));

  // Other names for the same wires on the sheet: b0 = shamt[0]; b1 = shamt[1]; b2 = shamt[2]; b3 = shamt[3];
  //   b4 = shamt[4]; shift_1[62:0] = extended_64[63:1]; stage_1[63:2] = shift_2; stage_2[63:4] = shift_4;
  //   stage_4[63:8] = shift_8; stage_8[63:16] = shift_16; stage_16[63:0] = res
endmodule

module S_L_L (
  input  [31:0] A,
  input  [4:0] shamt,
  output [63:0] res
);

  wire [63:0] extended_64;
  wire [63:2] shift_2;
  wire [63:4] shift_4;
  wire [63:8] shift_8;
  wire [63:16] shift_16;
  wire [63:48] stage_8;
  wire [63:56] stage_4;
  wire [63:60] stage_2;
  wire [63:62] stage_1;

  assign extended_64 = {{32{1'b0}}, A};  // Bit_Extender bit_extender_1
  Multiplexer #(.width(64)) multiplexer_1 (
    .in0({stage_8, shift_16}), .in1({shift_16, {16{1'b0}}}), .out(res), .sel(shamt[4]));
  Multiplexer #(.width(64)) multiplexer_2 (
    .in0(extended_64), .in1({extended_64[62:0], 1'b0}), .out({stage_1, shift_2}), .sel(shamt[0]));
  Multiplexer #(.width(64)) multiplexer_3 (
    .in0({stage_1, shift_2}), .in1({shift_2, 2'b00}), .out({stage_2, shift_4}), .sel(shamt[1]));
  Multiplexer #(.width(64)) multiplexer_4 (
    .in0({stage_2, shift_4}), .in1({shift_4, 4'b0000}), .out({stage_4, shift_8}), .sel(shamt[2]));
  Multiplexer #(.width(64)) multiplexer_5 (
    .in0({stage_4, shift_8}), .in1({shift_8, {8{1'b0}}}), .out({stage_8, shift_16}), .sel(shamt[3]));

  // Other names for the same wires on the sheet: b0 = shamt[0]; b1 = shamt[1]; b2 = shamt[2]; b3 = shamt[3];
  //   b4 = shamt[4]; shift_1[63:1] = extended_64[62:0]; stage_2[59:0] = shift_4; stage_4[55:0] = shift_8;
  //   stage_8[47:0] = shift_16; stage_1[61:0] = shift_2; stage_16[63:0] = res
endmodule

module C_L_O (
  input  [31:0] in1,
  input  S,
  input  clk,
  input  En,
  input  rst,
  output [4:0] cnt,
  output D
);

  wire CBO, CHECK, FINAL, INIT, not_1_out, not_2_out, not_3_out, or_1_out, or_2_out, or_3_out, or_4_out,
       R0_bit0, RN_eq_0, SHIFT, T0, T1, T2, T3, T4, T6;
  wire [4:0] adder_1_out, multiplexer_1_out, R1_q, RN_dec, RN_q;
  wire [31:0] multiplexer_2_out, R0_q;
  wire [63:0] c71_res;

  or or_1 (or_1_out, T0, SHIFT);
  D_Flip_Flop u_INIT (.D(T4), .clk(clk), .Q(INIT), .preset(rst));  // open: Qn, reset
  D_Flip_Flop u_CBO (.D(or_1_out), .clk(clk), .Q(CBO), .reset(rst));  // open: Qn, preset
  D_Flip_Flop u_SHIFT (.D(T6), .clk(clk), .Q(SHIFT), .reset(rst));  // open: Qn, preset
  D_Flip_Flop u_FINAL (.D(T1), .clk(clk), .Q(FINAL), .reset(rst));  // open: Qn, preset
  not not_1 (not_1_out, RN_eq_0);
  not not_2 (not_2_out, R0_bit0);
  not not_3 (not_3_out, S);
  and and_1 (T0, INIT, S);
  and and_2 (T1, CHECK, En, RN_eq_0);
  and and_3 (T2, CBO, R0_bit0);
  and and_4 (T3, CBO, not_2_out);
  and and_5 (T4, INIT, not_3_out);
  and and_6 (T6, CHECK, En, not_1_out);
  D_Flip_Flop u_CHECK (.D(CBO), .clk(clk), .Q(CHECK), .reset(rst));  // open: Qn, preset
  or or_2 (or_2_out, T0, SHIFT);
  Multiplexer #(.width(5)) multiplexer_1 (.in0({5{1'b1}}), .in1(RN_dec), .out(multiplexer_1_out), .sel(SHIFT));
  Register #(.width(5)) RN (.D(multiplexer_1_out), .en(or_2_out), .clk(clk), .Q(RN_q));  // open: clr
  or or_3 (or_3_out, T0, SHIFT);
  Multiplexer #(.width(32)) multiplexer_2 (.in0(in1), .in1(c71_res[31:0]), .out(multiplexer_2_out), .sel(SHIFT));
  Subtractor #(.width(5)) subtractor_1 (.a(RN_q), .b(5'b00001), .out(RN_dec));  // open: bin, bout
  Comparator #(.width(5)) comparator_1 (.a(RN_q), .b({5{1'b0}}), .eq(RN_eq_0));  // open: gt, lt
  Register #(.width(32)) R0 (.D(multiplexer_2_out), .en(or_3_out), .clk(clk), .Q(R0_q));  // open: clr
  or or_4 (or_4_out, T3, T0);
  and and_7 (R0_bit0, 1'b1, R0_q[0]);
  Register #(.width(5)) R1 (.D(adder_1_out), .en(T2), .clk(clk), .Q(R1_q), .clr(or_4_out));
  Register #(.width(5)) R2 (.D(R1_q), .en(T1), .clk(clk), .Q(cnt), .clr(rst));
  Register #(.width(1)) RD (.D(1'b1), .en(T1), .clk(clk), .Q(D), .clr(T0));
  S_R_L c71 (.A(R0_q), .shamt(5'b00001), .res(c71_res));
  Adder #(.width(5)) adder_1 (.a(R1_q), .b(5'b00001), .out(adder_1_out));  // open: cin, cout
endmodule

module C_L_Z (
  input  [31:0] in1,
  input  S,
  input  clk,
  input  En,
  input  rst,
  output [4:0] cnt,
  output D
);

  wire CBO, CHECK, FINAL, INIT, not_1_out, not_2_out, not_3_out, not_4_out, or_1_out, or_2_out, or_3_out,
       or_4_out, R0_bit0, RN_eq_0, SHIFT, T0, T1, T2, T3, T4, T6;
  wire [4:0] adder_1_out, multiplexer_1_out, R1_q, RN_dec, RN_q;
  wire [31:0] multiplexer_2_out, R0_q;
  wire [63:0] c71_res;

  or or_1 (or_1_out, T0, SHIFT);
  D_Flip_Flop u_INIT (.D(T4), .clk(clk), .Q(INIT), .preset(rst));  // open: Qn, reset
  D_Flip_Flop u_CBO (.D(or_1_out), .clk(clk), .Q(CBO), .reset(rst));  // open: Qn, preset
  D_Flip_Flop u_SHIFT (.D(T6), .clk(clk), .Q(SHIFT), .reset(rst));  // open: Qn, preset
  D_Flip_Flop u_FINAL (.D(T1), .clk(clk), .Q(FINAL), .reset(rst));  // open: Qn, preset
  not not_1 (not_1_out, RN_eq_0);
  not not_2 (not_2_out, R0_bit0);
  not not_3 (not_3_out, S);
  and and_1 (T0, INIT, S);
  and and_2 (T1, CHECK, En, RN_eq_0);
  and and_3 (T2, CBO, R0_bit0);
  and and_4 (T3, CBO, not_2_out);
  and and_5 (T4, INIT, not_3_out);
  and and_6 (T6, CHECK, En, not_1_out);
  D_Flip_Flop u_CHECK (.D(CBO), .clk(clk), .Q(CHECK), .reset(rst));  // open: Qn, preset
  or or_2 (or_2_out, T0, SHIFT);
  Multiplexer #(.width(5)) multiplexer_1 (.in0({5{1'b1}}), .in1(RN_dec), .out(multiplexer_1_out), .sel(SHIFT));
  Register #(.width(5)) RN (.D(multiplexer_1_out), .en(or_2_out), .clk(clk), .Q(RN_q));  // open: clr
  or or_3 (or_3_out, T0, SHIFT);
  Multiplexer #(.width(32)) multiplexer_2 (.in0(in1), .in1(c71_res[31:0]), .out(multiplexer_2_out), .sel(SHIFT));
  Subtractor #(.width(5)) subtractor_1 (.a(RN_q), .b(5'b00001), .out(RN_dec));  // open: bin, bout
  Comparator #(.width(5)) comparator_1 (.a(RN_q), .b({5{1'b0}}), .eq(RN_eq_0));  // open: gt, lt
  Register #(.width(32)) R0 (.D(multiplexer_2_out), .en(or_3_out), .clk(clk), .Q(R0_q));  // open: clr
  or or_4 (or_4_out, T3, T0);
  not not_4 (not_4_out, R0_q[0]);
  Register #(.width(5)) R1 (.D(adder_1_out), .en(T2), .clk(clk), .Q(R1_q), .clr(or_4_out));
  Register #(.width(5)) R2 (.D(R1_q), .en(T1), .clk(clk), .Q(cnt), .clr(rst));
  and and_7 (R0_bit0, 1'b1, not_4_out);
  Register #(.width(1)) RD (.D(1'b1), .en(T1), .clk(clk), .Q(D), .clr(T0));
  S_R_L c71 (.A(R0_q), .shamt(5'b00001), .res(c71_res));
  Adder #(.width(5)) adder_1 (.a(R1_q), .b(5'b00001), .out(adder_1_out));  // open: cin, cout
endmodule

module ROTR2 (
  input  [31:0] A,
  input  [4:0] shamt,
  output [63:0] res
);

  wire [1:0] lsb2;
  wire [3:0] lsb4;
  wire [7:0] lsb8;
  wire [15:0] lsb16;
  wire [47:0] shift_16;
  wire [55:0] shift_8;
  wire [59:0] shift_4;
  wire [61:0] shift_2;
  wire [63:0] extended_64, stage_16;

  assign extended_64 = {{32{1'b0}}, A};  // Bit_Extender bit_extender_1
  Multiplexer #(.width(64)) multiplexer_1 (
    .in0({shift_16, lsb16}), .in1({lsb16, shift_16}), .out(stage_16), .sel(shamt[4]));
  Multiplexer #(.width(64)) multiplexer_2 (
    .in0(extended_64), .in1({extended_64[0], extended_64[63:1]}), .out({shift_2, lsb2}), .sel(shamt[0]));
  Multiplexer #(.width(64)) multiplexer_3 (
    .in0({shift_2, lsb2}), .in1({lsb2, shift_2}), .out({shift_4, lsb4}), .sel(shamt[1]));
  Multiplexer #(.width(64)) multiplexer_4 (
    .in0({shift_4, lsb4}), .in1({lsb4, shift_4}), .out({shift_8, lsb8}), .sel(shamt[2]));
  Multiplexer #(.width(64)) multiplexer_5 (
    .in0({shift_8, lsb8}), .in1({lsb8, shift_8}), .out({shift_16, lsb16}), .sel(shamt[3]));
  assign res[31:0] = stage_16[31:0] | stage_16[63:32];  // OR_Gate or_1, 32 bits wide

  assign res[63:32] = {32{1'b0}};

  // Other names for the same wires on the sheet: b0 = shamt[0]; b1 = shamt[1]; b2 = shamt[2]; b3 = shamt[3];
  //   b4 = shamt[4]; shift_1[63:0] = {extended_64[0], extended_64[63:1]}; lsb1 = extended_64[0];
  //   stage_1[63:0] = {shift_2, lsb2}; stage_2[63:0] = {shift_4, lsb4}; shift_4[63:60] = lsb4;
  //   stage_4[63:0] = {shift_8, lsb8}; shift_8[63:56] = lsb8; stage_8[63:0] = {shift_16, lsb16};
  //   shift_2[63:62] = lsb2; shift_16[63:48] = lsb16
endmodule

module Carry_Save_Adder (
  input  c_in,
  input  [63:0] a,
  input  [63:0] b,
  input  [63:0] c,
  output [63:0] res
);

  wire [63:0] and_1_out, and_2_out, and_3_out, carry_out, shifter_1_out, xor_1_out, xor_2_out;

  assign xor_1_out = b ^ c;  // XOR_Gate xor_1, 64 bits wide
  assign and_1_out = a & b;  // AND_Gate and_1, 64 bits wide
  assign and_2_out = a & c;  // AND_Gate and_2, 64 bits wide
  assign and_3_out = b & c;  // AND_Gate and_3, 64 bits wide
  assign xor_2_out = a ^ xor_1_out;  // XOR_Gate xor_2, 64 bits wide
  assign carry_out = and_1_out | and_2_out | and_3_out;  // OR_Gate carry, 64 bits wide
  Shifter #(.width(64)) shifter_1 (.in(carry_out), .\dist (6'b000001), .out(shifter_1_out));
  Carry_Select_Adder c22 (.c_in(c_in), .a(xor_2_out), .b(shifter_1_out), .res(res));
endmodule

module Carry_Select_Adder (
  input  c_in,
  input  [63:0] a,
  input  [63:0] b,
  output [63:0] res
);

  wire adder_1_cout, adder_2_cout, adder_3_cout, adder_4_cout, adder_5_cout, adder_6_cout, adder_8_cout,
       adder_9_cout, adder_10_cout, adder_11_cout, adder_12_cout, adder_13_cout, adder_14_cout,
       multiplexer_1_out, multiplexer_2_out, multiplexer_3_out, multiplexer_4_out, multiplexer_5_out,
       multiplexer_6_out;
  wire [7:0] adder_1_out, adder_2_out, adder_3_out, adder_4_out, adder_5_out, adder_6_out, adder_7_out,
       adder_9_out, adder_10_out, adder_11_out, adder_12_out, adder_13_out, adder_14_out, adder_15_out;

  Adder adder_1 (.a(a[15:8]), .b(b[15:8]), .out(adder_1_out), .cout(adder_1_cout));  // open: cin
  Adder adder_2 (.a(a[23:16]), .b(b[23:16]), .out(adder_2_out), .cout(adder_2_cout));  // open: cin
  Adder adder_3 (.a(a[31:24]), .b(b[31:24]), .out(adder_3_out), .cout(adder_3_cout));  // open: cin
  Adder adder_4 (.a(a[39:32]), .b(b[39:32]), .out(adder_4_out), .cout(adder_4_cout));  // open: cin
  Adder adder_5 (.a(a[47:40]), .b(b[47:40]), .out(adder_5_out), .cout(adder_5_cout));  // open: cin
  Adder adder_6 (.a(a[55:48]), .b(b[55:48]), .out(adder_6_out), .cout(adder_6_cout));  // open: cin
  Adder adder_7 (.a(a[63:56]), .b(b[63:56]), .out(adder_7_out));  // open: cin, cout
  Adder adder_8 (.a(a[7:0]), .b(b[7:0]), .out(res[7:0]), .cin(c_in), .cout(adder_8_cout));
  Adder adder_9 (.a(a[15:8]), .b(b[15:8]), .out(adder_9_out), .cin(1'b1), .cout(adder_9_cout));
  Adder adder_10 (.a(a[23:16]), .b(b[23:16]), .out(adder_10_out), .cin(1'b1), .cout(adder_10_cout));
  Adder adder_11 (.a(a[31:24]), .b(b[31:24]), .out(adder_11_out), .cin(1'b1), .cout(adder_11_cout));
  Adder adder_12 (.a(a[39:32]), .b(b[39:32]), .out(adder_12_out), .cin(1'b1), .cout(adder_12_cout));
  Adder adder_13 (.a(a[47:40]), .b(b[47:40]), .out(adder_13_out), .cin(1'b1), .cout(adder_13_cout));
  Adder adder_14 (.a(a[55:48]), .b(b[55:48]), .out(adder_14_out), .cin(1'b1), .cout(adder_14_cout));
  Adder adder_15 (.a(a[63:56]), .b(b[63:56]), .out(adder_15_out), .cin(1'b1));  // open: cout
  Multiplexer multiplexer_1 (.in0(adder_1_cout), .in1(adder_9_cout), .out(multiplexer_1_out), .sel(adder_8_cout));
  Multiplexer multiplexer_2 (.in0(adder_2_cout), .in1(adder_10_cout), .out(multiplexer_2_out), .sel(multiplexer_1_out));
  Multiplexer multiplexer_3 (.in0(adder_3_cout), .in1(adder_11_cout), .out(multiplexer_3_out), .sel(multiplexer_2_out));
  Multiplexer multiplexer_4 (.in0(adder_4_cout), .in1(adder_12_cout), .out(multiplexer_4_out), .sel(multiplexer_3_out));
  Multiplexer multiplexer_5 (.in0(adder_5_cout), .in1(adder_13_cout), .out(multiplexer_5_out), .sel(multiplexer_4_out));
  Multiplexer multiplexer_6 (.in0(adder_6_cout), .in1(adder_14_cout), .out(multiplexer_6_out), .sel(multiplexer_5_out));
  Multiplexer #(.width(8)) multiplexer_7 (.in0(adder_1_out), .in1(adder_9_out), .out(res[15:8]), .sel(adder_8_cout));
  Multiplexer #(.width(8)) multiplexer_8 (
    .in0(adder_2_out), .in1(adder_10_out), .out(res[23:16]), .sel(multiplexer_1_out));
  Multiplexer #(.width(8)) multiplexer_9 (
    .in0(adder_3_out), .in1(adder_11_out), .out(res[31:24]), .sel(multiplexer_2_out));
  Multiplexer #(.width(8)) multiplexer_10 (
    .in0(adder_4_out), .in1(adder_12_out), .out(res[39:32]), .sel(multiplexer_3_out));
  Multiplexer #(.width(8)) multiplexer_11 (
    .in0(adder_5_out), .in1(adder_13_out), .out(res[47:40]), .sel(multiplexer_4_out));
  Multiplexer #(.width(8)) multiplexer_12 (
    .in0(adder_6_out), .in1(adder_14_out), .out(res[55:48]), .sel(multiplexer_5_out));
  Multiplexer #(.width(8)) multiplexer_13 (
    .in0(adder_7_out), .in1(adder_15_out), .out(res[63:56]), .sel(multiplexer_6_out));
endmodule

module M_U_L (
  input  [31:0] a,
  input  [31:0] b,
  input  start,
  input  clk,
  output [63:0] res,
  output done
);

  wire comparator_1_eq, not_1_out;
  wire [3:0] adder_1_out, counter_q, multiplexer_4_out, multiplexer_8_out;
  wire [4:0] adder_2_out;
  wire [31:0] bit_extender_1_out, multiplexer_1_out, multiplexer_2_out, multiplexer_5_out, multiplexer_6_out,
       multiplicand_q, multiplier_q;
  wire [63:0] case_01_res, case_10_res, case_11_res, i2, i21, multiplexer_3_out, multiplexer_7_out, result,
       s_r_l_1_res, sum;

  Multiplexer #(.width(32)) multiplexer_1 (.in0(multiplicand_q), .in1(a), .out(multiplexer_1_out), .sel(start));
  Multiplexer #(.width(32)) multiplexer_2 (.in0(bit_extender_1_out), .in1(b), .out(multiplexer_2_out), .sel(start));
  Multiplexer #(.width(64)) multiplexer_3 (.in0(result), .in1({64{1'b0}}), .out(multiplexer_3_out), .sel(start));
  Multiplexer #(.width(4)) multiplexer_4 (.in0(adder_1_out), .in1(4'b0000), .out(multiplexer_4_out), .sel(start));
  Multiplexer #(.width(32)) multiplexer_5 (
    .in0(multiplexer_1_out), .in1(multiplicand_q), .out(multiplexer_5_out), .sel(done));
  Multiplexer #(.width(32)) multiplexer_6 (
    .in0(multiplexer_2_out), .in1(multiplier_q), .out(multiplexer_6_out), .sel(done));
  Multiplexer #(.width(64)) multiplexer_7 (.in0(multiplexer_3_out), .in1(sum), .out(multiplexer_7_out), .sel(done));
  Multiplexer #(.width(4)) multiplexer_8 (
    .in0(multiplexer_4_out), .in1(counter_q), .out(multiplexer_8_out), .sel(done));
  Register #(.width(32)) multiplicand (.D(multiplexer_5_out), .clk(clk), .Q(multiplicand_q));  // open: en, clr
  Register #(.width(32)) multiplier (.D(multiplexer_6_out), .clk(clk), .Q(multiplier_q));  // open: en, clr
  Register #(.width(64)) u_sum (.D(multiplexer_7_out), .clk(clk), .Q(sum));  // open: en, clr
  Register #(.width(4)) counter (.D(multiplexer_8_out), .clk(clk), .Q(counter_q));  // open: en, clr
  Comparator #(.mode("unsigned"), .width(4)) comparator_1 (
    .a(counter_q), .b(4'b1111), .eq(comparator_1_eq));  // open: gt, lt
  Adder #(.width(4)) adder_1 (.a(counter_q), .b(4'b0001), .out(adder_1_out));  // open: cin, cout
  Adder #(.width(5)) adder_2 (.a({counter_q, 1'b0}), .b(5'b00001), .out(adder_2_out));  // open: cin, cout
  Carry_Select_Adder case_01 (.c_in(1'b0), .a(i2), .b(sum), .res(case_01_res));
  Carry_Select_Adder case_10 (.c_in(1'b0), .a(i21), .b(sum), .res(case_10_res));
  Carry_Save_Adder case_11 (.c_in(1'b0), .a(sum), .b(i2), .c(i21), .res(case_11_res));
  Bit_Extender #(.in_width(64), .out_width(32), .\type ("zero")) bit_extender_1 (
    .in(s_r_l_1_res), .out(bit_extender_1_out));
  S_R_L s_r_l_1 (.A(multiplier_q), .shamt(5'b00010), .res(s_r_l_1_res));
  S_L_L c23 (.A(multiplicand_q), .shamt({counter_q, 1'b0}), .res(i2));
  S_L_L c24 (.A(multiplicand_q), .shamt(adder_2_out), .res(i21));
  Multiplexer #(.select(2), .width(64)) multiplexer_9 (
    .in0(sum), .in1(case_01_res), .in2(case_10_res), .in3(case_11_res), .out(result), .sel(multiplier_q[1:0]));
  not not_1 (not_1_out, start);
  and and_1 (done, comparator_1_eq, not_1_out);
  Multiplexer #(.width(64)) multiplexer_10 (.in0({64{1'b0}}), .in1(result), .out(res), .sel(done));

  // Notes on the sheet:
  //   a: initial=0x39f50473
  //   b: initial=0xdd7199ba
endmodule
