// Logisim project single_cycle.circ as structural Verilog: 2 circuits, main circuit insctruction_decode
module insctruction_decode (
  input  [31:0] instruction,
  output [5:0] funct,
  output [4:0] shamt,
  output [4:0] rd,
  output [4:0] rt,
  output [4:0] rs,
  output [5:0] opcode,
  output [15:0] immediate
);


  assign funct = instruction[5:0];
  assign immediate = instruction[15:0];
  assign opcode = instruction[31:26];
  assign rd = instruction[15:11];
  assign rs = instruction[25:21];
  assign rt = instruction[20:16];
  assign shamt = instruction[10:6];
endmodule

module main (
);

  insctruction_decode insctruction_decode_1 ();  // open: instruction, funct, shamt, rd, rt, rs, opcode, immediate
endmodule
