// Logisim project lib.circ as structural Verilog: 11 circuits, main circuit CselectA
module CselectA (
  input  c_in,
  input  [31:0] a,
  input  [31:0] b,
  output [63:0] res
);

  wire adder_1_cout, adder_2_cout, adder_3_cout, adder_4_cout, adder_5_cout, adder_6_cout, adder_7_cout,
       adder_8_cout, adder_9_cout, adder_10_cout, adder_11_cout, adder_12_cout, adder_13_cout, adder_14_cout,
       adder_15_cout, multiplexer_1_out, multiplexer_2_out, multiplexer_3_out, multiplexer_4_out,
       multiplexer_5_out, multiplexer_6_out;
  wire [3:0] adder_1_out, adder_2_out, adder_3_out, adder_4_out, adder_5_out, adder_6_out, adder_7_out,
       adder_9_out, adder_10_out, adder_11_out, adder_12_out, adder_13_out, adder_14_out, adder_15_out;

  Adder #(.width(4)) adder_1 (.a(a[7:4]), .b(b[7:4]), .out(adder_1_out), .cout(adder_1_cout));  // open: cin
  Adder #(.width(4)) adder_2 (.a(a[11:8]), .b(b[11:8]), .out(adder_2_out), .cout(adder_2_cout));  // open: cin
  Adder #(.width(4)) adder_3 (.a(a[15:12]), .b(b[15:12]), .out(adder_3_out), .cout(adder_3_cout));  // open: cin
  Adder #(.width(4)) adder_4 (.a(a[19:16]), .b(b[19:16]), .out(adder_4_out), .cout(adder_4_cout));  // open: cin
  Adder #(.width(4)) adder_5 (.a(a[23:20]), .b(b[23:20]), .out(adder_5_out), .cout(adder_5_cout));  // open: cin
  Adder #(.width(4)) adder_6 (.a(a[27:24]), .b(b[27:24]), .out(adder_6_out), .cout(adder_6_cout));  // open: cin
  Adder #(.width(4)) adder_7 (.a(a[31:28]), .b(b[31:28]), .out(adder_7_out), .cout(adder_7_cout));  // open: cin
  Adder #(.width(4)) adder_8 (.a(a[3:0]), .b(b[3:0]), .out(res[3:0]), .cin(c_in), .cout(adder_8_cout));
  Adder #(.width(4)) adder_9 (.a(a[7:4]), .b(b[7:4]), .out(adder_9_out), .cin(1'b1), .cout(adder_9_cout));
  Adder #(.width(4)) adder_10 (.a(a[11:8]), .b(b[11:8]), .out(adder_10_out), .cin(1'b1), .cout(adder_10_cout));
  Adder #(.width(4)) adder_11 (.a(a[15:12]), .b(b[15:12]), .out(adder_11_out), .cin(1'b1), .cout(adder_11_cout));
  Adder #(.width(4)) adder_12 (.a(a[19:16]), .b(b[19:16]), .out(adder_12_out), .cin(1'b1), .cout(adder_12_cout));
  Adder #(.width(4)) adder_13 (.a(a[23:20]), .b(b[23:20]), .out(adder_13_out), .cin(1'b1), .cout(adder_13_cout));
  Adder #(.width(4)) adder_14 (.a(a[27:24]), .b(b[27:24]), .out(adder_14_out), .cin(1'b1), .cout(adder_14_cout));
  Adder #(.width(4)) adder_15 (.a(a[31:28]), .b(b[31:28]), .out(adder_15_out), .cin(1'b1), .cout(adder_15_cout));
  Multiplexer multiplexer_1 (.in0(adder_1_cout), .in1(adder_9_cout), .out(multiplexer_1_out), .sel(adder_8_cout));
  Multiplexer multiplexer_2 (.in0(adder_2_cout), .in1(adder_10_cout), .out(multiplexer_2_out), .sel(multiplexer_1_out));
  Multiplexer multiplexer_3 (.in0(adder_3_cout), .in1(adder_11_cout), .out(multiplexer_3_out), .sel(multiplexer_2_out));
  Multiplexer multiplexer_4 (.in0(adder_4_cout), .in1(adder_12_cout), .out(multiplexer_4_out), .sel(multiplexer_3_out));
  Multiplexer multiplexer_5 (.in0(adder_5_cout), .in1(adder_13_cout), .out(multiplexer_5_out), .sel(multiplexer_4_out));
  Multiplexer multiplexer_6 (.in0(adder_6_cout), .in1(adder_14_cout), .out(multiplexer_6_out), .sel(multiplexer_5_out));
  Multiplexer multiplexer_7 (.in0(adder_7_cout), .in1(adder_15_cout), .out(res[32]), .sel(multiplexer_6_out));
  Multiplexer #(.width(4)) multiplexer_8 (.in0(adder_1_out), .in1(adder_9_out), .out(res[7:4]), .sel(adder_8_cout));
  Multiplexer #(.width(4)) multiplexer_9 (
    .in0(adder_2_out), .in1(adder_10_out), .out(res[11:8]), .sel(multiplexer_1_out));
  Multiplexer #(.width(4)) multiplexer_10 (
    .in0(adder_3_out), .in1(adder_11_out), .out(res[15:12]), .sel(multiplexer_2_out));
  Multiplexer #(.width(4)) multiplexer_11 (
    .in0(adder_4_out), .in1(adder_12_out), .out(res[19:16]), .sel(multiplexer_3_out));
  Multiplexer #(.width(4)) multiplexer_12 (
    .in0(adder_5_out), .in1(adder_13_out), .out(res[23:20]), .sel(multiplexer_4_out));
  Multiplexer #(.width(4)) multiplexer_13 (
    .in0(adder_6_out), .in1(adder_14_out), .out(res[27:24]), .sel(multiplexer_5_out));
  Multiplexer #(.width(4)) multiplexer_14 (
    .in0(adder_7_out), .in1(adder_15_out), .out(res[31:28]), .sel(multiplexer_6_out));

  assign res[63:33] = {31{1'b0}};
endmodule

module Fast_Multipilier (
  input  [31:0] A,
  input  [31:0] B,
  input  En,
  input  clk
);

  wire [63:0] se_1_o;

  Counter #(.max('hf), .width(4)) counter_1 (
    .load(En), .up(1'b0), .count(1'b1), .clk(clk), .D(4'b1111));  // open: clr, carry, Q
  SE se_1 (.A(A), .O(se_1_o));
  Multiplexer #(.select(2), .width(64)) multiplexer_1 (.in0({64{1'b0}}), .in1(se_1_o));  // open: in2, in3, out, sel

  // Other names for the same wires on the sheet: S = En
endmodule

module CSA (
  input  c_in,
  input  [31:0] a,
  input  [31:0] b,
  input  [31:0] c,
  output [63:0] res
);

  wire [31:0] and_1_out, and_2_out, and_3_out, carry_out, sum_out;
  wire [63:0] s_l_l_1_res;

  assign and_1_out = a & b;  // AND_Gate and_1, 32 bits wide
  assign and_2_out = a & c;  // AND_Gate and_2, 32 bits wide
  assign and_3_out = b & c;  // AND_Gate and_3, 32 bits wide
  ExactlyOne sum[31:0] (.out(sum_out), .in0(a), .in1(b), .in2(c));
  assign carry_out = and_1_out | and_2_out | and_3_out;  // OR_Gate carry, 32 bits wide
  S_L_L s_l_l_1 (.A(carry_out), .shamt(5'b00001), .res(s_l_l_1_res));
  CselectA cselecta_1 (.c_in(c_in), .a(sum_out), .b(s_l_l_1_res[31:0]), .res(res));
endmodule

module SE (
  input  [31:0] A,
  output [63:0] O
);


  assign O = {{33{A[31]}}, A[30:0]};
endmodule

module CLO (
  input  [31:0] in1,
  input  S,
  input  clk,
  input  En,
  input  rst,
  output [4:0] cnt,
  output D
);

  wire CBO, FINAL, INIT, not_1_out, not_2_out, not_3_out, not_4_out, not_5_out, or_1_out, or_2_out, or_3_out,
       or_4_out, R0_bit0, RN_eq_0, SHIFT, T0, T1, T2, T3, T4, T5;
  wire [4:0] adder_1_out, controlled_buffer_1_out, R1_q, RN_dec, RN_q;
  wire [31:0] controlled_buffer_3_out, R0_q;
  wire [63:0] s_r_l_1_res;

  or or_1 (or_1_out, T0, SHIFT);
  D_Flip_Flop u_INIT (.D(T4), .clk(clk), .Q(INIT), .preset(rst));  // open: Qn, reset
  D_Flip_Flop u_CBO (.D(or_1_out), .clk(clk), .Q(CBO), .reset(rst));  // open: Qn, preset
  D_Flip_Flop u_SHIFT (.D(T5), .clk(clk), .Q(SHIFT), .reset(rst));  // open: Qn, preset
  D_Flip_Flop u_FINAL (.D(T1), .clk(clk), .Q(FINAL), .reset(rst));  // open: Qn, preset
  not not_1 (not_1_out, RN_eq_0);
  not not_2 (not_2_out, RN_eq_0);
  not not_3 (not_3_out, R0_bit0);
  not not_4 (not_4_out, S);
  not not_5 (not_5_out, RN_eq_0);
  and and_1 (T0, INIT, S);
  and and_2 (T1, CBO, En, RN_eq_0);
  and and_3 (T2, CBO, not_1_out, R0_bit0);
  and and_4 (T3, CBO, not_2_out, not_3_out);
  and and_5 (T4, INIT, not_4_out);
  and and_6 (T5, CBO, not_5_out);
  assign controlled_buffer_1_out = T0 ? {5{1'b1}} : 5'bz;  // Controlled_Buffer controlled_buffer_1
  assign controlled_buffer_1_out = SHIFT ? RN_dec : 5'bz;  // Controlled_Buffer controlled_buffer_2
  or or_2 (or_2_out, T0, SHIFT);
  Register #(.width(5)) RN (.D(controlled_buffer_1_out), .en(or_2_out), .clk(clk), .Q(RN_q));  // open: clr
  or or_3 (or_3_out, T0, SHIFT);
  assign controlled_buffer_3_out = T0 ? in1 : 32'bz;  // Controlled_Buffer controlled_buffer_3
  assign controlled_buffer_3_out = SHIFT ? s_r_l_1_res[31:0] : 32'bz;  // Controlled_Buffer controlled_buffer_4
  Subtractor #(.width(5)) subtractor_1 (.a(RN_q), .b(5'b00001), .out(RN_dec));  // open: bin, bout
  Comparator #(.width(5)) comparator_1 (.a(RN_q), .b({5{1'b0}}), .eq(RN_eq_0));  // open: gt, lt
  Register #(.width(32)) R0 (.D(controlled_buffer_3_out), .en(or_3_out), .clk(clk), .Q(R0_q));  // open: clr
  or or_4 (or_4_out, T3, T0);
  and and_7 (R0_bit0, 1'b1, R0_q[0]);
  Register #(.width(5)) R1 (.D(adder_1_out), .en(T2), .clk(clk), .Q(R1_q), .clr(or_4_out));
  Register #(.width(5)) R2 (.D(R1_q), .en(T1), .clk(clk), .Q(cnt), .clr(rst));
  Register #(.width(1)) RD (.D(1'b1), .en(T1), .clk(clk), .Q(D), .clr(T0));
  S_R_L s_r_l_1 (.A(R0_q), .shamt(5'b00001), .res(s_r_l_1_res));
  Adder #(.width(5)) adder_1 (.a(R1_q), .b(5'b00001), .out(adder_1_out));  // open: cin, cout
endmodule

module CLZ (
  input  [31:0] in1,
  input  S,
  input  clk,
  input  En,
  input  rst,
  output [4:0] cnt,
  output D
);

  wire CBO, FINAL, INIT, not_1_out, not_2_out, not_3_out, not_4_out, not_5_out, not_6_out, or_1_out,
       or_2_out, or_3_out, or_4_out, R0_bit0, RN_eq_0, SHIFT, T0, T1, T2, T3, T4, T5;
  wire [4:0] adder_1_out, controlled_buffer_1_out, R1_q, RN_dec, RN_q;
  wire [31:0] controlled_buffer_3_out, R0_q;
  wire [63:0] s_r_l_1_res;

  or or_1 (or_1_out, T0, SHIFT);
  D_Flip_Flop u_INIT (.D(T4), .clk(clk), .Q(INIT), .preset(rst));  // open: Qn, reset
  D_Flip_Flop u_CBO (.D(or_1_out), .clk(clk), .Q(CBO), .reset(rst));  // open: Qn, preset
  D_Flip_Flop u_SHIFT (.D(T5), .clk(clk), .Q(SHIFT), .reset(rst));  // open: Qn, preset
  D_Flip_Flop u_FINAL (.D(T1), .clk(clk), .Q(FINAL), .reset(rst));  // open: Qn, preset
  not not_1 (not_1_out, RN_eq_0);
  not not_2 (not_2_out, RN_eq_0);
  not not_3 (not_3_out, R0_bit0);
  not not_4 (not_4_out, S);
  not not_5 (not_5_out, RN_eq_0);
  and and_1 (T0, INIT, S);
  and and_2 (T1, CBO, En, RN_eq_0);
  and and_3 (T2, CBO, not_1_out, R0_bit0);
  and and_4 (T3, CBO, not_2_out, not_3_out);
  and and_5 (T4, INIT, not_4_out);
  and and_6 (T5, CBO, not_5_out);
  assign controlled_buffer_1_out = T0 ? {5{1'b1}} : 5'bz;  // Controlled_Buffer controlled_buffer_1
  assign controlled_buffer_1_out = SHIFT ? RN_dec : 5'bz;  // Controlled_Buffer controlled_buffer_2
  or or_2 (or_2_out, T0, SHIFT);
  Register #(.width(5)) RN (.D(controlled_buffer_1_out), .en(or_2_out), .clk(clk), .Q(RN_q));  // open: clr
  or or_3 (or_3_out, T0, SHIFT);
  assign controlled_buffer_3_out = T0 ? in1 : 32'bz;  // Controlled_Buffer controlled_buffer_3
  assign controlled_buffer_3_out = SHIFT ? s_r_l_1_res[31:0] : 32'bz;  // Controlled_Buffer controlled_buffer_4
  Subtractor #(.width(5)) subtractor_1 (.a(RN_q), .b(5'b00001), .out(RN_dec));  // open: bin, bout
  Comparator #(.width(5)) comparator_1 (.a(RN_q), .b({5{1'b0}}), .eq(RN_eq_0));  // open: gt, lt
  Register #(.width(32)) R0 (.D(controlled_buffer_3_out), .en(or_3_out), .clk(clk), .Q(R0_q));  // open: clr
  or or_4 (or_4_out, T3, T0);
  not not_6 (not_6_out, R0_q[0]);
  Register #(.width(5)) R1 (.D(adder_1_out), .en(T2), .clk(clk), .Q(R1_q), .clr(or_4_out));
  Register #(.width(5)) R2 (.D(R1_q), .en(T1), .clk(clk), .Q(cnt), .clr(rst));
  and and_7 (R0_bit0, 1'b1, not_6_out);
  Register #(.width(1)) RD (.D(1'b1), .en(T1), .clk(clk), .Q(D), .clr(T0));
  S_R_L s_r_l_1 (.A(R0_q), .shamt(5'b00001), .res(s_r_l_1_res));
  Adder #(.width(5)) adder_1 (.a(R1_q), .b(5'b00001), .out(adder_1_out));  // open: cin, cout
endmodule

module S_L_L (
  input  [31:0] A,
  input  [4:0] shamt,
  output [63:0] res
);

  wire [63:0] extended_64;
  wire [63:2] shift_2;
  wire [63:4] shift_4;
  wire [63:7] shift_8;
  wire [63:16] shift_16;
  wire [63:48] stage_8;
  wire [63:57] stage_4;
  wire [63:60] stage_2;
  wire [63:62] stage_1;

  ZE ze_1 (.A(A), .O(extended_64));
  Multiplexer #(.width(64)) multiplexer_1 (
    .in0({stage_8, shift_16}), .in1({shift_16, {16{1'b0}}}), .out(res), .sel(shamt[4]));
  Multiplexer #(.width(64)) multiplexer_2 (
    .in0(extended_64), .in1({extended_64[62:0], 1'b0}), .out({stage_1, shift_2}), .sel(shamt[0]));
  Multiplexer #(.width(64)) multiplexer_3 (
    .in0({stage_1, shift_2}), .in1({shift_2, 2'b00}), .out({stage_2, shift_4}), .sel(shamt[1]));
  Multiplexer #(.width(64)) multiplexer_4 (
    .in0({stage_2, shift_4}), .in1({shift_4, 4'b0000}), .out({stage_4, shift_8}), .sel(shamt[2]));
  Multiplexer #(.width(64)) multiplexer_5 (
    .in0({stage_4, shift_8}), .in1({shift_8, {7{1'b0}}}), .out({stage_8, shift_16}), .sel(shamt[3]));

  // Other names for the same wires on the sheet: b0 = shamt[0]; b1 = shamt[1]; b2 = shamt[2]; b3 = shamt[3];
  //   b4 = shamt[4]; shift_1[63:1] = extended_64[62:0]; stage_2[59:0] = shift_4; stage_8[47:0] = shift_16;
  //   stage_1[61:0] = shift_2; stage_4[56:0] = shift_8; stage_16[63:0] = res
endmodule

module ZE (
  input  [31:0] A,
  output [63:0] O
);


  assign O = {{32{1'b0}}, A};
endmodule

module S_R_L (
  input  [31:0] A,
  input  [4:0] shamt,
  output [63:0] res
);

  wire [1:0] stage_1;
  wire [3:0] stage_2;
  wire [7:0] stage_4;
  wire [15:0] stage_8;
  wire [47:0] shift_16;
  wire [55:0] shift_8;
  wire [59:0] shift_4;
  wire [61:0] shift_2;
  wire [63:0] extended_64;

  ZE ze_1 (.A(A), .O(extended_64));
  Multiplexer #(.width(64)) multiplexer_1 (
    .in0({shift_16, stage_8}), .in1({{16{1'b0}}, shift_16}), .out(res), .sel(shamt[4]));
  Multiplexer #(.width(64)) multiplexer_2 (
    .in0(extended_64), .in1({1'b0, extended_64[63:1]}), .out({shift_2, stage_1}), .sel(shamt[0]));
  Multiplexer #(.width(64)) multiplexer_3 (
    .in0({shift_2, stage_1}), .in1({2'b00, shift_2}), .out({shift_4, stage_2}), .sel(shamt[1]));
  Multiplexer #(.width(64)) multiplexer_4 (
    .in0({shift_4, stage_2}), .in1({4'b0000, shift_4}), .out({shift_8, stage_4}), .sel(shamt[2]));
  Multiplexer #(.width(64)) multiplexer_5 (
    .in0({shift_8, stage_4}), .in1({{8{1'b0}}, shift_8}), .out({shift_16, stage_8}), .sel(shamt[3]));

  // Other names for the same wires on the sheet: b0 = shamt[0]; b1 = shamt[1]; b2 = shamt[2]; b3 = shamt[3];
  //   b4 = shamt[4]; shift_1[62:0] = extended_64[63:1]; stage_1[63:2] = shift_2; stage_2[63:4] = shift_4;
  //   stage_4[63:8] = shift_8; stage_8[63:16] = shift_16; stage_16[63:0] = res
endmodule

module S_R_A (
  input  [31:0] A,
  input  [4:0] shamt,
  output [63:0] res
);

  wire [1:0] stage_1;
  wire [3:0] stage_2;
  wire [7:0] stage_4;
  wire [15:0] stage_8;
  wire [63:0] extended_64, shift_2, shift_4, shift_8, shift_16;

  SE se_1 (.A(A), .O(extended_64));
  Multiplexer #(.width(64)) multiplexer_1 (
    .in0({shift_16[63], shift_16[46:0], stage_8}), .in1({{17{shift_16[63]}}, shift_16[46:0]}), .out(res),
    .sel(shamt[4]));
  Multiplexer #(.width(64)) multiplexer_2 (
    .in0(extended_64), .in1({{2{extended_64[63]}}, extended_64[62:1]}),
    .out({shift_2[63], shift_2[60:0], stage_1}), .sel(shamt[0]));
  Multiplexer #(.width(64)) multiplexer_3 (
    .in0({shift_2[63], shift_2[60:0], stage_1}), .in1({{3{shift_2[63]}}, shift_2[60:0]}),
    .out({shift_4[63], shift_4[58:0], stage_2}), .sel(shamt[1]));
  Multiplexer #(.width(64)) multiplexer_4 (
    .in0({shift_4[63], shift_4[58:0], stage_2}), .in1({{5{shift_4[63]}}, shift_4[58:0]}),
    .out({shift_8[63], shift_8[54:0], stage_4}), .sel(shamt[2]));
  Multiplexer #(.width(64)) multiplexer_5 (
    .in0({shift_8[63], shift_8[54:0], stage_4}), .in1({{9{shift_8[63]}}, shift_8[54:0]}),
    .out({shift_16[63], shift_16[46:0], stage_8}), .sel(shamt[3]));

  // Other names for the same wires on the sheet: b0 = shamt[0]; b1 = shamt[1]; b2 = shamt[2]; b3 = shamt[3];
  //   b4 = shamt[4]; shift_1[63:0] = {{2{extended_64[63]}}, extended_64[62:1]};
  //   stage_1[63:2] = {shift_2[63], shift_2[60:0]}; shift_2[62:61] = {2{shift_2[63]}};
  //   stage_2[63:4] = {shift_4[63], shift_4[58:0]}; shift_4[62:59] = {4{shift_4[63]}};
  //   stage_4[63:8] = {shift_8[63], shift_8[54:0]}; shift_8[62:55] = {8{shift_8[63]}};
  //   stage_8[63:16] = {shift_16[63], shift_16[46:0]}; shift_16[62:47] = {16{shift_16[63]}}; stage_16[63:0] = res
endmodule

module ROTR (
  input  [31:0] A,
  input  [4:0] shamt,
  output [63:0] res
);

  wire [1:0] lsb2;
  wire [3:0] lsb4;
  wire [7:0] lsb8;
  wire [15:0] lsb16;
  wire [47:0] shift_16;
  wire [55:0] shift_8;
  wire [59:0] shift_4;
  wire [61:0] shift_2;
  wire [63:0] extended_64, stage_16;

  ZE ze_1 (.A(A), .O(extended_64));
  Multiplexer #(.width(64)) multiplexer_1 (
    .in0({shift_16, lsb16}), .in1({lsb16, shift_16}), .out(stage_16), .sel(shamt[4]));
  Multiplexer #(.width(64)) multiplexer_2 (
    .in0(extended_64), .in1({extended_64[0], extended_64[63:1]}), .out({shift_2, lsb2}), .sel(shamt[0]));
  Multiplexer #(.width(64)) multiplexer_3 (
    .in0({shift_2, lsb2}), .in1({lsb2, shift_2}), .out({shift_4, lsb4}), .sel(shamt[1]));
  Multiplexer #(.width(64)) multiplexer_4 (
    .in0({shift_4, lsb4}), .in1({lsb4, shift_4}), .out({shift_8, lsb8}), .sel(shamt[2]));
  Multiplexer #(.width(64)) multiplexer_5 (
    .in0({shift_8, lsb8}), .in1({lsb8, shift_8}), .out({shift_16, lsb16}), .sel(shamt[3]));
  assign res[31:0] = stage_16[31:0] | stage_16[63:32];  // OR_Gate or_1, 32 bits wide

  assign res[63:32] = {32{1'b0}};

  // Other names for the same wires on the sheet: b0 = shamt[0]; b1 = shamt[1]; b2 = shamt[2]; b3 = shamt[3];
  //   b4 = shamt[4]; shift_1[63:0] = {extended_64[0], extended_64[63:1]}; lsb1 = extended_64[0];
  //   stage_1[63:0] = {shift_2, lsb2}; stage_2[63:0] = {shift_4, lsb4}; shift_4[63:60] = lsb4;
  //   stage_4[63:0] = {shift_8, lsb8}; shift_8[63:56] = lsb8; stage_8[63:0] = {shift_16, lsb16};
  //   shift_2[63:62] = lsb2; shift_16[63:48] = lsb16
endmodule
